// Logisim project computer.circ as structural Verilog: 2 circuits, main circuit SR Latch
module SR_Latch (
  input  R,
  input  S,
  output Q,
  output Q_prime
);

  nor nor_1 (Q, R, Q_prime);
  nor nor_2 (Q_prime, Q, S);

  // Notes on the sheet:
  //   S: pull=down
  //   R: pull=down
endmodule

module main (
);

  wire and_1_out, and_2_out, and_3_out, and_4_out, and_5_out, and_6_out, and_7_out, and_8_out, and_9_out,
       and_10_out, and_11_out, and_12_out, ART, CAR, clock_1_out, controlled_buffer_1_out, EXC, HALT_out, I0,
       I1, I2, I3, I4, I5, I6, I7, JMP, LD, LIN, LM1, LM2, multiplexer_4_out, nor_1_out, not_1_out, or_1_out,
       or_2_out, or_3_out, or_4_out, or_5_out, or_6_out, PEX, PLN, PM1, PM2, register_1_q, register_6_q, RST,
       sr_latch_1_q, sr_latch_2_q, STR;
  wire [2:0] counter_2_q;
  wire [7:0] adder_1_out, DI, DO, multiplexer_2_out, multiplexer_3_out, not_2_out;
  wire [15:0] ADR, counter_1_q, multiplexer_1_out;

  and and_1 (and_1_out, ~I0, ~I1, ~I2);  // AND_Gate
  nor nor_1 (nor_1_out, DI[0], DI[1], DI[2], DI[3], DI[4], DI[5], DI[6], DI[7]);
  Register #(.width(1)) register_1 (.D(nor_1_out), .Q(register_1_q), .clk(PEX));  // open: en, clr
  and and_2 (and_2_out, ~I0, I1, ~I2, CAR);  // AND_Gate
  and and_3 (and_3_out, I0, ~I1, ~I2, register_1_q);  // AND_Gate
  or or_1 (or_1_out, and_1_out, and_3_out, and_2_out, and_5_out, and_6_out);
  and and_4 (and_4_out, JMP, or_1_out);
  and and_5 (and_5_out, I0, I1, ~I2, ~register_1_q);  // AND_Gate
  and and_6 (and_6_out, ~I0, ~I1, I2, ~CAR);  // AND_Gate
  and and_7 (and_7_out, and_4_out, or_2_out);
  assign controlled_buffer_1_out = and_7_out ? 1'b1 : 1'bz;  // Controlled_Buffer controlled_buffer_1
  not not_1 (not_1_out, controlled_buffer_1_out);
  or or_2 (or_2_out, EXC, PEX);
  and and_8 (and_8_out, and_4_out, EXC);
  Button RESET (.out(RST));
  Counter #(.width(16), .max('hffff)) counter_1 (
    .load(controlled_buffer_1_out), .D(ADR), .count(not_1_out), .Q(counter_1_q), .clk(or_3_out), .clr(RST));  // open: carry
  or or_3 (or_3_out, and_8_out, or_4_out);
  or or_4 (or_4_out, PLN, PM1, PM2);
  and HALT (HALT_out, I0, I1, I2, I3, I4, I5, I6, I7);
  Multiplexer #(.width(16)) multiplexer_1 (
    .in0(counter_1_q), .in1(ADR), .out(multiplexer_1_out), .sel(sr_latch_1_q));  // open: en
  SR_Latch sr_latch_1 (.R(or_3_out), .S(PEX), .Q(sr_latch_1_q));  // open: Q_prime
  and and_9 (and_9_out, ~sr_latch_2_q, clock_1_out);  // AND_Gate
  SR_Latch sr_latch_2 (.R(RST), .S(HALT_out), .Q(sr_latch_2_q));  // open: Q_prime
  Clock clock_1 (.out(clock_1_out));
  and and_10 (and_10_out, STR, or_5_out);
  or or_5 (or_5_out, EXC, PEX);
  Multiplexer #(.width(8)) multiplexer_2 (.in0(DO), .in1(not_2_out), .out(multiplexer_2_out), .sel(I0));  // open: en
  assign not_2_out = ~DO;  // NOT_Gate not_2, 8 bits wide
  Multiplexer #(.width(8)) multiplexer_3 (.in0(DO), .in1(adder_1_out), .out(multiplexer_3_out), .sel(ART));  // open: en
  Register register_2 (.D(multiplexer_3_out), .Q(DI), .clk(and_11_out), .clr(RST));  // open: en
  and and_11 (and_11_out, or_6_out, EXC);
  or or_6 (or_6_out, LD, ART);
  Counter #(.width(3), .max('h7)) counter_2 (
    .Q(counter_2_q), .clk(and_9_out), .clr(RST));  // open: load, D, count, carry
  RAM #(.addrWidth(16), .bus("separate")) ram_1 (
    .addr(multiplexer_1_out), .din(DI), .data(DO), .str(and_10_out), .clk(EXC));  // open: sel, ld, clr
  Multiplexer multiplexer_4 (.in0(I0), .in1(register_6_q), .out(multiplexer_4_out), .sel(I1));  // open: en
  Adder adder_1 (.a(multiplexer_2_out), .b(DI), .out(adder_1_out), .cin(multiplexer_4_out), .cout(CAR));
  Decoder #(.select(3)) decoder_1 (
    .out0(PLN), .out1(LIN), .out2(PM1), .out3(LM1), .out4(PM2), .out5(LM2), .out6(PEX), .out7(EXC),
    .sel(counter_2_q));  // open: en
  Register register_3 (.D(DO), .Q({I7, I6, I5, I4, I3, I2, I1, I0}), .clk(LIN), .clr(RST));  // open: en
  Register register_4 (.D(DO), .Q(ADR[15:8]), .clk(LM1));  // open: en, clr
  Register register_5 (.D(DO), .Q(ADR[7:0]), .clk(LM2));  // open: en, clr
  Register #(.width(1)) register_6 (.D(CAR), .Q(register_6_q), .clk(and_12_out), .clr(RST));  // open: en
  and and_12 (and_12_out, ART, EXC);
  and and_13 (ART, ~I4, I5, ~I6, ~I7);  // AND_Gate
  and and_14 (LD, ~I0, ~I1, ~I2, ~I3, I4, ~I5, ~I6, ~I7);  // AND_Gate
  and and_15 (STR, I0, ~I1, ~I2, ~I3, I4, ~I5, ~I6, ~I7);  // AND_Gate
  and and_16 (JMP, I4, I5, ~I6, ~I7);  // AND_Gate

  // Other names for the same wires on the sheet: INS[7:0] = {I7, I6, I5, I4, I3, I2, I1, I0}

  // Notes on the sheet:
  //   OPCODES
  //   LOAD
  //   0x10
  //   0x11
  //   STORE
  //   0x20
  //   ADD
  //   0x21
  //   SUB
  //   0x22
  //   0x23
  //   JUMP
  //   0x30
  //   0x31
  //   0x32
  //   0x33
  //   0x34
  //   HALT
  //   0xff
  //   JUMP
  //   ADD CARRY
  //   SUB BORROW
  //   JUMP IF ZERO
  //   JUMP IF CARRY
  //   JUMP IF NOT ZERO
  //   JUMP IF NOT CARRY
  //   CLOCK
  //   ALU
endmodule
